# Fritzing sketch circuit (saved by Fritzing 0.9.3b)

parts:
  Maker_UNO = Maker Uno (Arduino Uno Compatible)
  WATER_PUMP1 = water pump/motor  # not connected
  HC-05 = Bluetooth HC-05 Macho
  Relay = KF-301 Relay [package=THT]

nets:
  N1: Maker_UNO.D2, HC-05.RXD
  N2: Maker_UNO.D3_PWM, HC-05.TXD
  5V: Maker_UNO.5V, HC-05.VCC, Relay.power
  GND: Maker_UNO.GND, HC-05.GND, Relay.ground

notes:
  Arduino compatible board

custom parts:
  Maker Uno (Arduino Uno Compatible): Maker Uno, an Arduino UNO compatible board designed and developed specially for students to learn coding and microcontroller. We named it Maker UNO to encourage everyone to be a maker by getting started with this amazing board. Oh! BTW, it is PURPLE color.
  water pump/motor: WATER PUMP BY ARDUBLOCKTR
  KF-301 Relay: KF-301
